# Fritzing sketch flopppy jukebox (saved by Fritzing 0.9.3b)
breadboards: 1

parts:
  Bauteil1 = Arduino Nano (Rev3.0)
  Bauteil2 = Arduino Nano (Rev3.0)
  Power_plug1 = Power plug
  S1 = Pushbutton [package="[THT]"]
  S2 = Pushbutton [package="[THT]"]
  S3 = Pushbutton [package="[THT]"]
  S4 = Pushbutton [package="[THT]"]
  Bauteil4 = MicroSD Card Module
  Bauteil5 = BME280 Breakout
  LCD1 = LCD screen  # not connected
  J3 = shrouded pin header, 34 pins [form="♂ (shrouded male)"]
  J4 = male pin header, 4 pins [form="♂ (male)"]
  J5 = shrouded pin header, 34 pins [form="♂ (shrouded male)"]
  J6 = male pin header, 4 pins [form="♂ (male)"]
  J7 = shrouded pin header, 34 pins [form="♂ (shrouded male)"]
  J8 = male pin header, 4 pins [form="♂ (male)"]
  R1 = Resistor [tolerance=±5% resistance=220 package=THT]
  R2 = Resistor [tolerance=±5% resistance=1k package=THT]
  R3 = Resistor [tolerance=±5% resistance=1k package=THT]
  R4 = Resistor [tolerance=±5% resistance=1k package=THT]
  R5 = Resistor [tolerance=±5% resistance=1k package=THT]
  LED1 = Super Flux RGB LED (com. anode)
  LED2 = Super Flux RGB LED (com. anode)
  LED3 = Super Flux RGB LED (com. anode)

nets:
  N1: Bauteil1.D1/TX, Bauteil2.D0/RX
  N2: Bauteil1.D0/RX, Bauteil2.D1/TX
  N3: Bauteil1.D4, Bauteil4.CS
  N4: Bauteil1.D6, S1.Pin_1, S1.Pin_2, R3.Pin_0
  N5: Bauteil1.D7, S2.Pin_1, S2.Pin_2, R2.Pin_0
  N6: Bauteil1.D8, S3.Pin_1, S3.Pin_2, R4.Pin_0
  N7: Bauteil1.D9, S4.Pin_1, S4.Pin_2, R5.Pin_0
  N8: Bauteil1.D11/MOSI, Bauteil4.MOSI
  N9: Bauteil1.D12/MISO, Bauteil4.MISO
  VIN: Bauteil1.VIN, Bauteil2.VIN, Power_plug1.VCC, S1.Pin_3, S1.Pin_4, S2.Pin_3, S2.Pin_4, S3.Pin_3, S3.Pin_4, S4.Pin_3, S4.Pin_4, Bauteil4.VCC, Bauteil5.3.3V, J4.pin4, J6.pin4, J8.pin4
  GND: Bauteil1.GND, Bauteil2.GND, Power_plug1.GND, Bauteil4.GND, Bauteil5.GND, J3.pin9, J3.pin10, J4.pin3, J5.pin9, J5.pin10, J5.pin12, J5.pin13, J5.pin22, J5.pin23, J6.pin3, J7.pin9, J7.pin10, J8.pin3, R1.Pin_1, R2.Pin_1, R3.Pin_1, R4.Pin_1, R5.Pin_1
  N10: Bauteil1.A5, Bauteil5.SCK/SCL
  N11: Bauteil1.A4, Bauteil5.SDI/SDA
  N12: Bauteil1.D13/SCK, Bauteil4.SCK
  N13: Bauteil2.D2, J7.pin25
  N14: Bauteil2.D3, J7.pin26
  N15: Bauteil2.D4, J5.pin25
  N16: Bauteil2.D5, J5.pin26
  N17: Bauteil2.D6, J3.pin25
  N18: Bauteil2.D7, J3.pin26
  N19: Bauteil2.D8, LED3.red_cathode
  N20: Bauteil2.D9, LED3.green_cathode
  N21: Bauteil2.D10, LED3.blue_cathode
  N22: Bauteil2.A5, LED2.blue_cathode
  N23: Bauteil2.A4, LED2.green_cathode
  N24: Bauteil2.A3, LED2.red_cathode
  N25: Bauteil2.A2, LED1.blue_cathode
  N26: Bauteil2.A1, LED1.green_cathode
  N27: Bauteil2.A0, LED1.red_cathode
  N28: J3.pin6, J3.pin29
  N29: J5.pin6, J5.pin29
  N30: J7.pin6, J7.pin29
  N31: R1.Pin_0, LED1.common_anode, LED2.common_anode, LED3.common_anode
